# Fritzing sketch sht31-basic (saved by Fritzing 0.9.10b)
breadboards: 1

parts:
  J1 = SHT3X [form="♂ (male)" package=THT]
  M1 = ESP32-Nodemcu-32s [part_number=ESP32-Nodemcu-32s]

nets:
  VIN: J1.VIN, M1.5V
  GND: J1.GND, M1.GND
  N1: J1.SCL/T, M1.GPIO22
  N2: J1.SDA/RH, M1.GPIO21

custom parts:
  SHT3X: SHT31 SHT31-D Temperature & Humidity Sensor Breakout
  ESP32-Nodemcu-32s: The DOIT Esp32 DevKit v1 is one of the development board created by DOIT to evaluate the ESP-WROOM-32 module. It is based on the ESP32 microcontroller that boasts Wifi, Bluetooth, Ethernet and Low Power support all in a single chip. This module is 42pins long (2x21) and 11 pins width.
