# Fritzing sketch 1bt-control (saved by Fritzing 0.9.10b)

parts:
  M1 = ESP32-Nodemcu-32s [part_number=ESP32-Nodemcu-32s]
  U1 = WS2812 RGB LED matrix 1x8
  S1 = Pushbutton [package="[THT]"]

nets:
  N1: M1.GND#13, S1.Pin_2
  5V: M1.5V, U1.VCC
  N2: M1.GPIO2, S1.Pin_3, S1.Pin_4
  N3: M1.GPIO16, U1.DIN
  N4: M1.GND#37, U1.GND

custom parts:
  ESP32-Nodemcu-32s: The DOIT Esp32 DevKit v1 is one of the development board created by DOIT to evaluate the ESP-WROOM-32 module. It is based on the ESP32 microcontroller that boasts Wifi, Bluetooth, Ethernet and Low Power support all in a single chip. This module is 42pins long (2x21) and 11 pins width.
  WS2812 RGB LED matrix 1x8: WS2812 matrix 1x8
