# Fritzing sketch test1 (saved by Fritzing 0.9.10b)

parts:
  M1 = ESP32-Nodemcu-32s [part_number=ESP32-Nodemcu-32s]
  元件1 = Soil Moisture Sensor

nets:
  N1: M1.GPIO36, 元件1.SIG
  5V: M1.5V, 元件1.VCC
  GND: M1.GND, 元件1.GND

custom parts:
  ESP32-Nodemcu-32s: The DOIT Esp32 DevKit v1 is one of the development board created by DOIT to evaluate the ESP-WROOM-32 module. It is based on the ESP32 microcontroller that boasts Wifi, Bluetooth, Ethernet and Low Power support all in a single chip. This module is 42pins long (2x21) and 11 pins width.
