# Fritzing sketch test (saved by Fritzing 0.9.10b)
breadboards: 1

parts:
  M1 = ESP32-Nodemcu-32s [part_number=ESP32-Nodemcu-32s]
  U1 = Sharp Dust Sensor [part_number=GP2Y1010AU0F]
  R1 = Resistor [tolerance=±5% power=0.25 resistance=150 package=THT]
  C1 = Electrolytic Capacitor [capacitance=220µF voltage=35V package="100 mil [THT, electrolytic]"]

nets:
  N1: M1.GPIO36, U1.Vo
  N2: M1.GPIO12, U1.LED
  N3: M1.GND#13, U1.LED-GND, U1.S-GND, C1.-
  5V: M1.5V, U1.VCC, R1.Pin_1
  N4: U1.V-LED, R1.Pin_0, C1.+

notes:
  pin
  1w Vled to Resistor
  2B LED-GND to GND
  3G LED to DIO
  4Y S-GND to GND
  5B out to input
  6R Vcc to 5V

custom parts:
  ESP32-Nodemcu-32s: The DOIT Esp32 DevKit v1 is one of the development board created by DOIT to evaluate the ESP-WROOM-32 module. It is based on the ESP32 microcontroller that boasts Wifi, Bluetooth, Ethernet and Low Power support all in a single chip. This module is 42pins long (2x21) and 11 pins width.
  Sharp Dust Sensor: Sharp GP2Y1010AU0F Dust Sensor
